# Fritzing sketch Schéma-Final (saved by Fritzing 0.9.3b)
breadboards: 1

parts:
  Composant1 = Arduino Uno (Rev3)
  R1 = Resistor [tolerance=±5% resistance=1M package=THT]
  L1 = Inductor [package="400 mil [THT]"]
  R2 = Resistor [tolerance=±5% resistance=10k package=THT]
  R3 = Resistor [tolerance=±5% resistance=220 package=THT]
  LED1 = LED - 5mm [color="Green (565nm)" package="5 mm [THT]"]
  R4 = Resistor [tolerance=±5% resistance=220 package=THT]
  LED2 = LED - 5mm [color="Yellow (585nm)" package="5 mm [THT]"]
  R5 = Resistor [tolerance=±5% resistance=150 package=THT]
  LED3 = LED - 5mm [color="Red (633nm)" package="5 mm [THT]"]
  R6 = Resistor [tolerance=±5% resistance=220 package=THT]
  LED4 = LED - 5mm [color="White (4500K)" package="5 mm [THT]"]

nets:
  N1: Composant1.A0, R1.Pin_0, L1.pin_0
  N2: Composant1.D9_PWM, R2.Pin_0
  N3: Composant1.D11_PWM/MOSI, R6.Pin_0
  N4: Composant1.D2, R3.Pin_0
  N5: Composant1.D4, R4.Pin_0
  N6: Composant1.D6_PWM, R5.Pin_0
  N7: Composant1.GND, R1.Pin_1, LED1.cathode, LED2.cathode, LED3.cathode, LED4.cathode
  N8: L1.pin_1, R2.Pin_1
  N9: R3.Pin_1, LED1.anode
  N10: R4.Pin_1, LED2.anode
  N11: R5.Pin_1, LED3.anode
  N12: R6.Pin_1, LED4.anode
